# Fritzing sketch uploading_circuit (saved by Fritzing 0.9.8b)

parts:
  Mod1 = ESP32 - CAM [part_number="Short between IO0 and GND during uploding"]
  USBTTL1 = USB TTL Serial Cable

nets:
  5V: Mod1.5V, USBTTL1.5V
  GND: Mod1.GND, Mod1.IO0, USBTTL1.GND
  N1: Mod1.VOT, USBTTL1.RX
  N2: Mod1.VOR, USBTTL1.TX

custom parts:
  ESP32 - CAM: The ESP32-CAM has a very competitive small-size camera module that can operate independently as a minimum system with a footprint of only 27*40.5*4.5mm and a deep sleep current of up to 6mA.
